# Fritzing sketch ArduinoHat (saved by Fritzing 0.9.3b)

parts:
  Part4 = Adafruit Perma-Proto HAT [part_number="Adafruit #2314 and #2310"]
  Part5 = Adafruit Trinket 5V
  R11 = PHOTOCELL [package=photocell]
  R17 = Resistor [tolerance=±5% resistance=10k package="2512 [SMD]"]
  R16 = Resistor [tolerance=±5% resistance=220 package="2512 [SMD]"]
  R18 = Resistor [tolerance=±5% resistance=22k package="2512 [SMD]"]
  Q2 = NPN-Transistor [package="TO92 [THT]"]
  R19 = Resistor [tolerance=±5% resistance=330 package="2512 [SMD]"]
  J2 = female pin header, 6 pins [form="♀ (female)"]
  R20 = Resistor [tolerance=±5% resistance=570 package="2512 [SMD]"]
  R15 = Resistor [tolerance=±5% resistance=10k package="2512 [SMD]"]
  LED1 = smd LED [color="Red (633nm)" package="0603 [SMD]"]
  J4 = Basic Servo
  J5 = Dagu DGServo 9g header (male) [package=THT]
  proto1 = Adafruit_PermaProto_1_4_Board
  LED3 = smd LED [color="Infrared (850nm)" package="1206 [SMD]"]  # not connected
  LED6 = smd LED [color="Infrared (850nm)" package="1206 [SMD]"]  # not connected
  LED7 = smd LED [color="Infrared (850nm)" package="1206 [SMD]"]  # not connected
  LED8 = smd LED [color="Infrared (850nm)" package="1206 [SMD]"]  # not connected
  LED9 = smd LED [color="Infrared (850nm)" package="1206 [SMD]"]  # not connected
  LED10 = smd LED [color="Infrared (850nm)" package="1206 [SMD]"]  # not connected
  LED14 = smd LED [color="Infrared (850nm)" package="1206 [SMD]"]  # not connected
  LED15 = smd LED [color="Infrared (850nm)" package="1206 [SMD]"]  # not connected
  LED16 = smd LED [color="Infrared (850nm)" package="1206 [SMD]"]  # not connected
  LED17 = smd LED [color="Infrared (850nm)" package="1206 [SMD]"]  # not connected
  LED18 = smd LED [color="Infrared (850nm)" package="1206 [SMD]"]  # not connected
  LED19 = smd LED [color="Infrared (850nm)" package="1206 [SMD]"]  # not connected
  R21 = Resistor [tolerance=±5% resistance=27 package="2512 [SMD]"]  # not connected
  R22 = Resistor [tolerance=±5% resistance=27 package="2512 [SMD]"]  # not connected
  R23 = Resistor [tolerance=±5% resistance=27 package="2512 [SMD]"]  # not connected
  R24 = Resistor [tolerance=±5% resistance=27 package="2512 [SMD]"]  # not connected
  R25 = Resistor [tolerance=±5% resistance=150 package="2512 [SMD]"]  # not connected
  R26 = Resistor [tolerance=±5% resistance=150 package="2512 [SMD]"]  # not connected
  LED20 = smd LED [color="Infrared (850nm)" package="1206 [SMD]"]  # not connected
  LED21 = smd LED [color="Infrared (850nm)" package="1206 [SMD]"]  # not connected

nets:
  N1: Part4.TXD, Part4.N$9#197
  N2: Part4.RXD, Part4.N$53#333
  N3: Part4.GPIO18, Part4.N$13#220
  N4: Part4.5.0V, Part4.N$2#161, Part4.N$14#222, Part4.N$17#231
  N5: Part4.GND, Part4.N$3#166, Part4.N$15#227, Part4.N$18#236, Part4.N$46#296, Part4.N$49#311
  N6: Part4.N$2#163, Part5.VBAT
  N7: Part4.N$3#168, Part5.GND
  N8: Part4.N$4#171, Part4.N$22#258
  N9: Part4.N$4#173, Part5.#4
  N10: Part4.N$5#176, R16.Pin_0
  N11: Part4.N$5#178, Part5.#3
  N12: Part4.N$6, Part5.RESET
  N13: Part4.N$9#196, R16.Pin_1
  N14: Part4.N$13#219, J4.pulse, J5.gnd
  VCC: Part4.N$14#224, J4.vcc, J5.Vcc
  N15: Part4.N$15#229, J4.gnd, J5.pulse
  N16: Part4.N$17#233, Part4.N$20#246
  N17: Part4.N$17#234, J2.pin1, proto1.connectorW12
  N18: Part4.N$18#237, R15.Pin_0
  N19: Part4.N$19#244, J2.pin2, proto1.connectorX12
  N20: Part4.N$19#245, Part4.N$44#290
  N21: Part4.N$20#248, Part4.N$21#251
  N22: Part4.N$20#249, R11.P$1, J2.pin3
  N23: Part4.N$21#254, J2.pin5, LED1.anode
  N24: Part4.N$22#257, R15.Pin_1
  N25: Part4.N$22#259, R11.P$2, J2.pin4
  N26: Part4.N$23#264, Part4.N$39#270
  N27: Part4.N$23#265, J2.pin6, LED1.cathode
  N28: Part4.N$39#268, R20.Pin_1
  N29: Part4.N$44#288, R20.Pin_0
  N30: Part4.N$44#289, Q2.E
  N31: Part4.N$45#293, R19.Pin_1
  N32: Part4.N$45#294, Q2.B
  N33: Part4.N$46#299, Q2.C
  N34: Part4.N$49#312, R18.Pin_1
  N35: Part4.N$50#318, R19.Pin_0
  N36: Part4.N$50#319, Part4.N$60#368
  N37: Part4.N$53#332, R18.Pin_0
  N38: Part4.N$53#334, R17.Pin_1
  N39: Part4.N$57, Part5.+5V
  N40: Part4.N$58#359, R17.Pin_0
  N41: Part4.N$58#360, Part5.#2
  N42: Part4.N$59, Part5.#0
  N43: Part4.N$60#370, Part5.#1
  N44: Part4.N$61, Part5.VBUS
  N45: proto1.connectorA7, proto1.connectorX7
  N46: proto1.connectorA9, proto1.connectorW9
  N47: proto1.connectorB2, proto1.connectorB3
  N48: proto1.connectorB12, proto1.connectorB13
  N49: proto1.connectorD4, proto1.connectorD5
  N50: proto1.connectorD10, proto1.connectorD11
  N51: proto1.connectorD14, proto1.connectorD15
  N52: proto1.connectorE1, proto1.connectorW3
  N53: proto1.connectorF1, proto1.connectorY3
  N54: proto1.connectorG4, proto1.connectorG5
  N55: proto1.connectorG10, proto1.connectorG11
  N56: proto1.connectorG14, proto1.connectorG15
  N57: proto1.connectorI2, proto1.connectorI3
  N58: proto1.connectorI9, proto1.connectorY9
  N59: proto1.connectorI12, proto1.connectorI13
  N60: proto1.connectorJ7, proto1.connectorY7
  N61: proto1.connectorW14, proto1.connectorY14
  N62: proto1.connectorX14, proto1.connectorZ14

notes:
  Front IR LED panel
  Status LED to mimic IR LED brightness
  Servo to control the camera
  Diagram uses a 5 V Trinket

custom parts:
  Adafruit Perma-Proto HAT: To kick off the Adafruit HAT party, we have this Perma-Proto inspired plug in daughter board. It has a grid of 0.1" prototyping soldering holes for attaching chips, resistors, LED, potentiometers and more. The holes are connected underneath with traces to mimic the solderless breadboards you're familiar. There's also long power strips for +3V, +5V and Ground connections to the Pi. Near the top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
  Adafruit Trinket 5V: Trinket may be small, but do not be fooled by its size! It's a tiny microcontroller board, built around the Atmel ATtiny85, a little chip with a lot of power. We wanted to design a microcontroller board that was small enough to fit into any project, and low cost enough to use without hesitation. Perfect for when you don't want to give up your expensive dev-board and you aren't willing to take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
