# Fritzing sketch WatctowerHAT (saved by Fritzing 0.9.3b)

parts:
  proto2 = Adafruit_PermaProto_1_4_Board
  Part6 = Adafruit Perma-Proto HAT [part_number="Adafruit #2314 and #2310"]
  R27 = PHOTOCELL [package=photocell]
  R30 = Resistor [tolerance=±5% resistance=220 package="2512 [SMD]"]
  LED22 = smd LED [color="Red (633nm)" package="0603 [SMD]"]  # not connected
  J7 = Basic Servo
  R33 = Resistor [tolerance=±5% resistance=10k package="2512 [SMD]"]
  LED24 = smd LED [color="Infrared (850nm)" package="1206 [SMD]"]  # not connected
  LED25 = smd LED [color="Infrared (850nm)" package="1206 [SMD]"]  # not connected
  LED28 = smd LED [color="Infrared (850nm)" package="1206 [SMD]"]  # not connected
  LED32 = smd LED [color="Infrared (850nm)" package="1206 [SMD]"]  # not connected
  R36 = Resistor [tolerance=±5% resistance=4.7 package="2512 [SMD]"]  # not connected
  Q4 = NPN-Transistor [package="TO92 [THT]"]
  U1 = ATTiny84 [package=dip]
  J9 = female pin header, 2 pins [form="♀ (female)"]
  F1 = Fan - Ventilador [package=THT]
  J12 = female pin header, 2 pins [form="♀ (female)"]
  J13 = female pin header, 2 pins [form="♀ (female)"]
  R40 = Resistor [tolerance=±5% resistance=820 package="2512 [SMD]"]
  J16 = male pin header, 2 pins [form="♂ (male)"]
  J17 = male pin header, 2 pins [form="♂ (male)"]
  J23 = female pin header, 3 pins [form="♀ (female)"]
  C2 = Ceramic Capacitor [capacitance=100nF package="100 mil [THT, multilayer]"]
  LED37 = smd LED [color="Infrared (850nm)" package="1206 [SMD]"]  # not connected
  LED38 = smd LED [color="Infrared (850nm)" package="1206 [SMD]"]  # not connected
  LED39 = smd LED [color="Infrared (850nm)" package="1206 [SMD]"]  # not connected
  LED40 = smd LED [color="Infrared (850nm)" package="1206 [SMD]"]  # not connected
  R42 = Resistor [tolerance=±5% resistance=4.7 package="2512 [SMD]"]  # not connected
  LED41 = smd LED [color="Infrared (850nm)" package="1206 [SMD]"]  # not connected
  R43 = Resistor [tolerance=±5% resistance=4.7 package="2512 [SMD]"]  # not connected
  LED43 = smd LED [color="Infrared (850nm)" package="1206 [SMD]"]  # not connected
  LED44 = smd LED [color="Infrared (850nm)" package="1206 [SMD]"]  # not connected
  R44 = Resistor [tolerance=±5% resistance=4.7 package="2512 [SMD]"]  # not connected
  J24 = male pin header, 2 pins [form="♂ (male)"]
  Q6 = NPN-Transistor [package="TO92 [THT]"]
  J18 = male pin header, 3 pins [form="♂ (male)"]
  R45 = Resistor [tolerance=±5% resistance=10k package="2512 [SMD]"]
  R46 = Resistor [tolerance=±5% resistance=10k package="2512 [SMD]"]
  R48 = Resistor [tolerance=±5% resistance=10k package="2512 [SMD]"]
  R49 = Resistor [tolerance=±5% resistance=10k package="2512 [SMD]"]
  R50 = Resistor [tolerance=±5% resistance=10k package="2512 [SMD]"]
  R51 = Resistor [tolerance=±5% resistance=10k package="2512 [SMD]"]
  R52 = Resistor [tolerance=±5% resistance=1k package="2512 [SMD]"]
  J25 = female pin header, 1 pin [form="♀ (female)"]
  J26 = female pin header, 1 pin [form="♀ (female)"]
  LED45 = smd LED [color="Infrared (850nm)" package="1206 [SMD]"]  # not connected
  J27 = female pin header, 2 pins [form="♀ (female)"]  # not connected

nets:
  N1: proto2.connectorA2, R27.P$1
  N2: proto2.connectorA3, proto2.connectorW3
  N3: proto2.connectorA9, proto2.connectorW9
  N4: proto2.connectorB12, proto2.connectorB13
  N5: proto2.connectorD4, proto2.connectorD5
  N6: proto2.connectorD6, proto2.connectorD7
  N7: proto2.connectorD10, proto2.connectorD11
  N8: proto2.connectorD14, proto2.connectorD15
  N9: proto2.connectorG4, proto2.connectorG5
  N10: proto2.connectorG6, proto2.connectorG7
  N11: proto2.connectorG10, proto2.connectorG11
  N12: proto2.connectorG14, proto2.connectorG15
  N13: proto2.connectorI2, proto2.connectorZ2
  N14: proto2.connectorI3, proto2.connectorY3
  N15: proto2.connectorI9, proto2.connectorY9
  N16: proto2.connectorI12, proto2.connectorI13
  N17: proto2.connectorW1, proto2.connectorY1
  N18: proto2.connectorW12, Part6.N$58#356, J9.pin2, J17.pin2
  N19: proto2.connectorX1, proto2.connectorZ1
  N20: proto2.connectorX12, Part6.N$60#366, J9.pin1, J17.pin1
  N21: Part6.TXD, Part6.N$13#216
  N22: Part6.RXD, Part6.N$14#221
  N23: Part6.GPIO17, Part6.N$23#264
  N24: Part6.GPIO27, Part6.N$21#255
  N25: Part6.GPIO22, Part6.N$22#260
  N26: Part6.GPIO23, Part6.N$39#268
  N27: Part6.GPIO5, Part6.N$62#376
  N28: Part6.3.3V, Part6.N$51#321, C2.0, R52.Pin_0
  N29: Part6.GND, Part6.N$4#171, Part6.N$12#211, Part6.N$61#371, R33.Pin_0, C2.1
  N30: Part6.5.0V, Part6.N$1#156, Part6.N$5#176
  N31: Part6.N$1#159, F1.5V, J13.pin1, J16.pin1
  N32: Part6.N$2#162, Q6.E
  N33: Part6.N$2#164, F1.GND, J13.pin2, J16.pin2
  N34: Part6.N$3#167, Q6.B
  N35: Part6.N$3#170, R40.Pin_0
  N36: Part6.N$4#172, Q6.C
  N37: Part6.N$4#174, J7.gnd, J23.pin1, J18.pin1
  N38: Part6.N$5#179, J7.vcc, J23.pin2, J18.pin2
  N39: Part6.N$5#180, Part6.N$58#360
  N40: Part6.N$6#182, Part6.N$18#236
  N41: Part6.N$6#184, J7.pulse, J23.pin3, J18.pin3
  N42: Part6.N$6#185, U1.pin8
  N43: Part6.N$7#189, Part6.N$49#315
  N44: Part6.N$7#190, U1.pin10
  N45: Part6.N$8#191, Part6.N$17#231
  N46: Part6.N$8#195, U1.pin9
  N47: Part6.N$9#198, R46.Pin_0
  N48: Part6.N$9#200, U1.pin11
  N49: Part6.N$10#204, R45.Pin_0
  N50: Part6.N$10#205, U1.pin12
  N51: Part6.N$11, U1.pin13
  N52: Part6.N$12#215, U1.pin14
  N53: Part6.N$13#218, R46.Pin_1
  N54: Part6.N$14#224, R45.Pin_1
  N55: Part6.N$17#233, R49.Pin_0
  N56: Part6.N$18#237, R48.Pin_0
  N57: Part6.N$19#244, R50.Pin_0
  N58: Part6.N$19#245, Part6.N$53#334
  N59: Part6.N$21#253, R49.Pin_1
  N60: Part6.N$22#257, R48.Pin_1
  N61: Part6.N$23#265, R50.Pin_1
  N62: Part6.N$39#269, R51.Pin_1
  N63: Part6.N$44#288, Part6.N$57#353
  N64: Part6.N$44#289, R51.Pin_0
  N65: Part6.N$49#313, R33.Pin_1
  N66: Part6.N$49#314, J12.pin2, J24.pin1
  N67: Part6.N$50#318, R52.Pin_1
  N68: Part6.N$50#319, J25.pin1, J26.pin1
  N69: Part6.N$51#324, J12.pin1, J24.pin2
  N70: Part6.N$51#325, U1.pin1
  N71: Part6.N$52, U1.pin2
  N72: Part6.N$53#335, U1.pin4
  N73: Part6.N$54, U1.pin3
  N74: Part6.N$55, U1.pin5
  N75: Part6.N$56#349, R30.Pin_1
  N76: Part6.N$56#350, U1.pin6
  N77: Part6.N$57#355, U1.pin7
  N78: Part6.N$59#363, Q4.B
  N79: Part6.N$59#364, R30.Pin_0
  N80: Part6.N$60#368, Q4.E
  N81: Part6.N$61#373, Q4.C
  N82: Part6.N$62#379, R40.Pin_1

notes:
  Front panel containing:
  - 12 IR LEDs (4 100mA circuits)
  - 1 status LED at 3.3mA
  - 1 photoresistor
  Servo to move the camera
  GPIO 17, 27, 22, and 23 are ICSP Lines
  GPIO 5 controls the case fan

custom parts:
  Adafruit Perma-Proto HAT: To kick off the Adafruit HAT party, we have this Perma-Proto inspired plug in daughter board. It has a grid of 0.1" prototyping soldering holes for attaching chips, resistors, LED, potentiometers and more. The holes are connected underneath with traces to mimic the solderless breadboards you're familiar. There's also long power strips for +3V, +5V and Ground connections to the Pi. Near the top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
  ATTiny84: Atmel ATTiny84 processor. 8 ADC pins, 4 PWM pins. Available in either 10MHz or 20MHz. The last 2 pin numbers refer to arduino. D6 = Arduino 6, A6 = Arduino A6 example: PA6 (SDA/MOSI/OC1A/DI/AD6/PCINT6/D6/A6) NOTE: This part is diagrammed to suit the MIT HLT ATTiny84 core at https://github.com/damellis/attiny/
  Fan - Ventilador: Ventilador de 2 pines, se encuentra comunmente en computadoras de escritorio
